# Fritzing sketch wiring (saved by Fritzing 0.9.3b)

parts:
  Bauteil3 = Arduino Pro Mini (5V)
  R1 = Resistor [tolerance=±1% resistance=330 package="2010 [SMD]"]
  LED2 = LED - 3mm [color="Red (633nm)" package="3 mm [THT]"]
  S3 = Momentary Switch [package=ksa_sealed_tac_switch]
  VCC1 = Battery
  Stepdown_Voltage1 = Polulu Stepdown Voltage [part_number=D24V25F3,D24V25F5]
  R3 = Resistor [tolerance=±1% resistance=470k package="2010 [SMD]"]
  R4 = Resistor [tolerance=±1% resistance=100k package="2010 [SMD]"]
  U1 = CC1101 [part_number=CC1101]
  Bauteil4 = HX711 Weighing Sensor Module
  Load_Cell1 = Load Cell - Red/white/black/green

nets:
  N1: Bauteil3.A4, Bauteil4.CK/TX
  N2: Bauteil3.A5, Bauteil4.DO/RX
  GND: Bauteil3.GND, LED2.cathode, S3.3, VCC1.-, Stepdown_Voltage1.GND, U1.2, Bauteil4.GND
  VCC: Bauteil3.VCC, Stepdown_Voltage1.VOut, U1.1, Bauteil4.VCC
  N3: Bauteil3.A1, R3.Pin_0, R4.Pin_1
  N4: Bauteil3.SCK, U1.4
  N5: Bauteil3.MISO, U1.5
  N6: Bauteil3.MOSI, U1.3
  N7: Bauteil3.D10, U1.8
  N8: Bauteil3.D8, S3.1
  N9: Bauteil3.D5, R4.Pin_0
  N10: Bauteil3.D4, R1.Pin_1
  N11: Bauteil3.D2, U1.7
  N12: R1.Pin_0, LED2.anode
  N13: VCC1.+, Stepdown_Voltage1.VIn, R3.Pin_1
  N14: Bauteil4.E+, Load_Cell1.wire1
  N15: Bauteil4.E-, Load_Cell1.wire3
  N16: Bauteil4.A+, Load_Cell1.wire2
  N17: Bauteil4.A-, Load_Cell1.wire4

custom parts:
  Polulu Stepdown Voltage: Polulu Stepdown Voltage 3V3 or 5V, 2.5A
  Load Cell - Red/white/black/green: A rectangle load cell/weighting pressure Sensor with four wires - Red, white, black, green. Normally corresponding with E+, E-, A+, A- respectively.
